// Logisim project ARA_SoSe_25_Schaltungen.circ as structural Verilog
module _2_1_Multiplexer__Kap__2__S__68 (
  input  e0,
  input  sel,
  input  e1,
  output f
);

  wire and_1_out, and_2_out;

  and and_1 (and_1_out, e0, ~sel);  // AND_Gate
  and and_2 (and_2_out, sel, e1);
  or or_1 (f, and_1_out, and_2_out);
endmodule

module _2_1_Multiplexer__Variante (
  input  s,
  input  e0,
  input  e1,
  output out_4
);

  wire _0_out, _1_out, not_1_out;

  not not_1 (not_1_out, s);
  and _0 (_0_out, e0, not_1_out);
  and _1 (_1_out, e1, s);
  or or_1 (out_4, _0_out, _1_out);
endmodule

module _4_1_Multiplexer (
  input  s0,
  input  s1,
  input  e0,
  input  e1,
  input  e2,
  input  e3,
  output out_7
);

  wire _00_out, _01_out, _10_out, _11_out, not_1_out, not_2_out;

  not not_1 (not_1_out, s1);
  not not_2 (not_2_out, s0);
  and _00 (_00_out, e0, not_2_out, not_1_out);
  and _01 (_01_out, e1, not_2_out, s1);
  and _10 (_10_out, e2, s0, not_1_out);
  and _11 (_11_out, e3, s0, s1);
  or or_1 (out_7, _00_out, _01_out, _10_out, _11_out);
endmodule

module _1_2_Demultiplexer__Kap__2__S__70 (
  input  e,
  input  sel,
  output f0,
  output f1
);

  or or_1 (f0, e, sel);
  or or_2 (f1, e, ~sel);  // OR_Gate
endmodule

module \_3_Bit_Identitäts_Komparator__Kap__2__S_78  (
  input  x1,
  input  y1,
  input  x2,
  input  y2,
  input  x3,
  input  y3,
  output f
);

  wire xnor_1_out, xnor_2_out, xnor_3_out;

  xnor xnor_1 (xnor_1_out, x1, y1);
  xnor xnor_2 (xnor_2_out, x2, y2);
  xnor xnor_3 (xnor_3_out, x3, y3);
  and and_1 (f, xnor_1_out, xnor_2_out, xnor_3_out);
endmodule

module \_1_Bit_Größen_Komparator__Kap__2__S__79  (
  input  x,
  input  y,
  output x_y,
  output x_y_2,
  output x_y_3
);

  and and_1 (x_y, x, ~y);  // AND_Gate
  and and_2 (x_y_3, ~x, y);  // AND_Gate
  nor nor_1 (x_y_2, x_y, x_y_3);
endmodule

module Halbaddierer__Kap__2__S__80 (
  input  a,
  input  b,
  output S,
  output C
);

  wire and_1_out, and_2_out;

  and and_1 (and_1_out, a, ~b);  // AND_Gate
  and and_2 (and_2_out, ~a, b);  // AND_Gate
  and and_3 (C, a, b);
  or or_1 (S, and_1_out, and_2_out);
endmodule

module Volladdierer__Kap__2__S__81 (
  input  a,
  input  b,
  input  c,
  output C_2,
  output S
);

  wire halbaddierer_kap_2_s_80_1_c, halbaddierer_kap_2_s_80_1_s, halbaddierer_kap_2_s_80_2_c;

  or or_1 (C_2, halbaddierer_kap_2_s_80_1_c, halbaddierer_kap_2_s_80_2_c);
  Halbaddierer__Kap__2__S__80 halbaddierer_kap_2_s_80_1 (
    .a(a), .b(b), .S(halbaddierer_kap_2_s_80_1_s), .C(halbaddierer_kap_2_s_80_1_c));
  Halbaddierer__Kap__2__S__80 halbaddierer_kap_2_s_80_2 (
    .a(halbaddierer_kap_2_s_80_1_s), .b(c), .S(S), .C(halbaddierer_kap_2_s_80_2_c));
endmodule

module Ripple_Carry_Addierer__Kap__2__S__82 (
  input  a3,
  input  a2,
  input  a1,
  input  a0,
  input  b3,
  input  b2,
  input  b1,
  input  b0,
  output S4,
  output S3,
  output S2,
  output S1,
  output S0
);

  wire halbaddierer_kap_2_s_80_1_c, volladdierer_kap_2_s_81_2_c_2, volladdierer_kap_2_s_81_3_c_2;

  Volladdierer__Kap__2__S__81 volladdierer_kap_2_s_81_1 (
    .a(a3), .b(b3), .c(volladdierer_kap_2_s_81_2_c_2), .C_2(S4), .S(S3));
  Volladdierer__Kap__2__S__81 volladdierer_kap_2_s_81_2 (
    .a(a2), .b(b2), .c(volladdierer_kap_2_s_81_3_c_2), .C_2(volladdierer_kap_2_s_81_2_c_2), .S(S2));
  Volladdierer__Kap__2__S__81 volladdierer_kap_2_s_81_3 (
    .a(a1), .b(b1), .c(halbaddierer_kap_2_s_80_1_c), .C_2(volladdierer_kap_2_s_81_3_c_2), .S(S1));
  Halbaddierer__Kap__2__S__80 halbaddierer_kap_2_s_80_1 (.a(a0), .b(b0), .S(S0), .C(halbaddierer_kap_2_s_80_1_c));
endmodule

module Addierer_Subtrahierer__Kap__2__S__85 (
  input  a3,
  input  a2,
  input  a1,
  input  a0,
  input  b3,
  input  b2,
  input  b1,
  input  b0,
  input  _0___ADD,
  output S4,
  output S3,
  output S2,
  output S1,
  output S0
);

  wire n2_1_multiplexer_kap_2_s_68_1_f, n2_1_multiplexer_kap_2_s_68_2_f, n2_1_multiplexer_kap_2_s_68_3_f,
       n2_1_multiplexer_kap_2_s_68_4_f, not_1_out, not_2_out, not_3_out, not_4_out,
       volladdierer_kap_2_s_81_2_c_2, volladdierer_kap_2_s_81_3_c_2, volladdierer_kap_2_s_81_4_c_2;

  not not_1 (not_1_out, b3);
  _2_1_Multiplexer__Kap__2__S__68 u_2_1_multiplexer_kap_2_s_68_1 (
    .e0(b3), .sel(_0___ADD), .e1(not_1_out), .f(n2_1_multiplexer_kap_2_s_68_1_f));
  Volladdierer__Kap__2__S__81 volladdierer_kap_2_s_81_1 (
    .a(a3), .b(n2_1_multiplexer_kap_2_s_68_1_f), .c(volladdierer_kap_2_s_81_2_c_2), .C_2(S4), .S(S3));
  not not_2 (not_2_out, b2);
  _2_1_Multiplexer__Kap__2__S__68 u_2_1_multiplexer_kap_2_s_68_2 (
    .e0(b2), .sel(_0___ADD), .e1(not_2_out), .f(n2_1_multiplexer_kap_2_s_68_2_f));
  Volladdierer__Kap__2__S__81 volladdierer_kap_2_s_81_2 (
    .a(a2), .b(n2_1_multiplexer_kap_2_s_68_2_f), .c(volladdierer_kap_2_s_81_3_c_2),
    .C_2(volladdierer_kap_2_s_81_2_c_2), .S(S2));
  not not_3 (not_3_out, b1);
  _2_1_Multiplexer__Kap__2__S__68 u_2_1_multiplexer_kap_2_s_68_3 (
    .e0(b1), .sel(_0___ADD), .e1(not_3_out), .f(n2_1_multiplexer_kap_2_s_68_3_f));
  Volladdierer__Kap__2__S__81 volladdierer_kap_2_s_81_3 (
    .a(a1), .b(n2_1_multiplexer_kap_2_s_68_3_f), .c(volladdierer_kap_2_s_81_4_c_2),
    .C_2(volladdierer_kap_2_s_81_3_c_2), .S(S1));
  not not_4 (not_4_out, b0);
  _2_1_Multiplexer__Kap__2__S__68 u_2_1_multiplexer_kap_2_s_68_4 (
    .e0(b0), .sel(_0___ADD), .e1(not_4_out), .f(n2_1_multiplexer_kap_2_s_68_4_f));
  Volladdierer__Kap__2__S__81 volladdierer_kap_2_s_81_4 (
    .a(a0), .b(n2_1_multiplexer_kap_2_s_68_4_f), .c(_0___ADD), .C_2(volladdierer_kap_2_s_81_4_c_2), .S(S0));

  // Notes on the sheet:
  //   1 = SUB
endmodule

module _3_Bit_Multiplizierer__Kap_2__S_89 (
  input  a2,
  input  a1,
  input  a0,
  input  b0,
  input  b1,
  input  b2,
  output p5,
  output p4,
  output p3,
  output p2,
  output p1,
  output p0
);

  wire and_1_out, and_2_out, and_3_out, and_4_out, and_5_out, and_6_out, and_7_out, and_8_out, and_9_out,
       volladdierer_kap_2_s_81_2_c_2, volladdierer_kap_2_s_81_2_s, volladdierer_kap_2_s_81_3_c_2,
       volladdierer_kap_2_s_81_4_c_2, volladdierer_kap_2_s_81_4_s, volladdierer_kap_2_s_81_5_c_2,
       volladdierer_kap_2_s_81_5_s, volladdierer_kap_2_s_81_6_c_2, volladdierer_kap_2_s_81_6_s,
       volladdierer_kap_2_s_81_7_c_2, volladdierer_kap_2_s_81_8_c_2, volladdierer_kap_2_s_81_9_c_2;

  and and_1 (and_1_out, b2, a2);
  and and_2 (and_2_out, b1, a2);
  Volladdierer__Kap__2__S__81 volladdierer_kap_2_s_81_1 (
    .a(volladdierer_kap_2_s_81_2_c_2), .b(and_1_out), .c(volladdierer_kap_2_s_81_3_c_2), .C_2(p5), .S(p4));
  and and_3 (and_3_out, b0, a2);
  Volladdierer__Kap__2__S__81 volladdierer_kap_2_s_81_2 (
    .a(volladdierer_kap_2_s_81_4_c_2), .b(and_2_out), .c(volladdierer_kap_2_s_81_5_c_2),
    .C_2(volladdierer_kap_2_s_81_2_c_2), .S(volladdierer_kap_2_s_81_2_s));
  and and_4 (and_4_out, b2, a1);
  Volladdierer__Kap__2__S__81 volladdierer_kap_2_s_81_3 (
    .a(volladdierer_kap_2_s_81_2_s), .b(and_4_out), .c(volladdierer_kap_2_s_81_7_c_2),
    .C_2(volladdierer_kap_2_s_81_3_c_2), .S(p3));
  Volladdierer__Kap__2__S__81 volladdierer_kap_2_s_81_4 (
    .a(1'b0), .b(and_3_out), .c(volladdierer_kap_2_s_81_6_c_2), .C_2(volladdierer_kap_2_s_81_4_c_2),
    .S(volladdierer_kap_2_s_81_4_s));
  and and_5 (and_5_out, b1, a1);
  Volladdierer__Kap__2__S__81 volladdierer_kap_2_s_81_5 (
    .a(volladdierer_kap_2_s_81_4_s), .b(and_5_out), .c(volladdierer_kap_2_s_81_8_c_2),
    .C_2(volladdierer_kap_2_s_81_5_c_2), .S(volladdierer_kap_2_s_81_5_s));
  and and_6 (and_6_out, b2, a0);
  and and_7 (and_7_out, b0, a1);
  Volladdierer__Kap__2__S__81 volladdierer_kap_2_s_81_6 (
    .a(1'b0), .b(and_7_out), .c(volladdierer_kap_2_s_81_9_c_2), .C_2(volladdierer_kap_2_s_81_6_c_2),
    .S(volladdierer_kap_2_s_81_6_s));
  and and_8 (and_8_out, b1, a0);
  Volladdierer__Kap__2__S__81 volladdierer_kap_2_s_81_7 (
    .a(volladdierer_kap_2_s_81_5_s), .b(and_6_out), .c(1'b0), .C_2(volladdierer_kap_2_s_81_7_c_2), .S(p2));
  and and_9 (and_9_out, b0, a0);
  Volladdierer__Kap__2__S__81 volladdierer_kap_2_s_81_8 (
    .a(volladdierer_kap_2_s_81_6_s), .b(and_8_out), .c(1'b0), .C_2(volladdierer_kap_2_s_81_8_c_2), .S(p1));
  Volladdierer__Kap__2__S__81 volladdierer_kap_2_s_81_9 (
    .a(1'b0), .b(and_9_out), .c(1'b0), .C_2(volladdierer_kap_2_s_81_9_c_2), .S(p0));
endmodule

module RS_Flipflop_NOR__Kap__3__S__28 (
  input  R,
  input  S,
  output Q,
  output nQ
);

  nor nor_1 (Q, R, nQ);
  nor nor_2 (nQ, Q, S);
endmodule

module RS_Flipflop_mit_Pegelsteuerung__Kap__3__S__30 (
  input  S,
  input  C,
  input  R,
  output Q,
  output nQ
);

  wire and_1_out, and_2_out;

  and and_1 (and_1_out, S, C);
  and and_2 (and_2_out, C, R);
  RS_Flipflop_NOR__Kap__3__S__28 rs_flipflop_nor_kap_3_s_28_1 (.R(and_2_out), .S(and_1_out), .Q(Q), .nQ(nQ));
endmodule

module D_Flipflop_mit_Pegelsteuerung__Kap__3__S__34 (
  input  D,
  input  C,
  output Q,
  output nQ
);

  wire not_1_out;

  not not_1 (not_1_out, D);
  RS_Flipflop_mit_Pegelsteuerung__Kap__3__S__30 rs_flipflop_mit_pegelsteuerung_kap_3_s_30_1 (
    .S(D), .C(C), .R(not_1_out), .Q(Q), .nQ(nQ));
endmodule

module RS_Master_Slave_Flipflop_mit_negativer_Taktflankensteuerung__Kap__3__S__36 (
  input  S,
  input  C,
  input  R,
  output Q,
  output nQ
);

  wire and_1_out, and_2_out, and_3_out, and_4_out, not_1_out, rs_flipflop_nor_kap_3_s_28_1_nq,
       rs_flipflop_nor_kap_3_s_28_1_q;

  and and_1 (and_1_out, S, C);
  and and_2 (and_2_out, C, R);
  RS_Flipflop_NOR__Kap__3__S__28 rs_flipflop_nor_kap_3_s_28_1 (
    .R(and_2_out), .S(and_1_out), .Q(rs_flipflop_nor_kap_3_s_28_1_q), .nQ(rs_flipflop_nor_kap_3_s_28_1_nq));
  not not_1 (not_1_out, C);
  and and_3 (and_3_out, rs_flipflop_nor_kap_3_s_28_1_q, not_1_out);
  and and_4 (and_4_out, not_1_out, rs_flipflop_nor_kap_3_s_28_1_nq);
  RS_Flipflop_NOR__Kap__3__S__28 rs_flipflop_nor_kap_3_s_28_2 (.R(and_4_out), .S(and_3_out), .Q(Q), .nQ(nQ));

  // Notes on the sheet:
  //   Master
  //   Slave
endmodule

module RS_Master_Slave_Flipflop_mit_positiver_Taktflankensteuerung (
  input  S,
  input  C,
  input  R,
  output Q,
  output nQ
);

  wire and_1_out, and_2_out, and_3_out, and_4_out, not_1_out, rs_flipflop_nor_kap_3_s_28_1_nq,
       rs_flipflop_nor_kap_3_s_28_1_q;

  not not_1 (not_1_out, C);
  and and_1 (and_1_out, S, not_1_out);
  and and_2 (and_2_out, not_1_out, R);
  RS_Flipflop_NOR__Kap__3__S__28 rs_flipflop_nor_kap_3_s_28_1 (
    .R(and_2_out), .S(and_1_out), .Q(rs_flipflop_nor_kap_3_s_28_1_q), .nQ(rs_flipflop_nor_kap_3_s_28_1_nq));
  and and_3 (and_3_out, rs_flipflop_nor_kap_3_s_28_1_q, C);
  and and_4 (and_4_out, C, rs_flipflop_nor_kap_3_s_28_1_nq);
  RS_Flipflop_NOR__Kap__3__S__28 rs_flipflop_nor_kap_3_s_28_2 (.R(and_4_out), .S(and_3_out), .Q(Q), .nQ(nQ));

  // Notes on the sheet:
  //   Master
  //   Slave
endmodule

module RS_Master_Slave_Flipflop_aus_NAND_Gattern__kap__3__S__39 (
  input  S,
  input  C,
  input  R,
  output Q,
  output nQ
);

  wire nand_1_out, nand_2_out, nand_3_out, nand_4_out, nand_5_out, nand_6_out, nand_7_out;

  nand nand_1 (nand_1_out, C, S);
  nand nand_2 (nand_2_out, R, C);
  nand nand_3 (nand_3_out, nand_1_out, nand_4_out);
  nand nand_4 (nand_4_out, nand_3_out, nand_2_out);
  nand nand_5 (nand_5_out, C, C);
  nand nand_6 (nand_6_out, nand_5_out, nand_3_out);
  nand nand_7 (nand_7_out, nand_4_out, nand_5_out);
  nand nand_8 (Q, nand_6_out, nQ);
  nand nand_9 (nQ, Q, nand_7_out);
endmodule

module D_Master_Slave_Flipflop_mit_Taktflankensteuerung__Kap__3__S__41 (
  input  D,
  input  C,
  output Q,
  output nQ
);

  wire not_1_out;

  not not_1 (not_1_out, D);
  RS_Master_Slave_Flipflop_mit_positiver_Taktflankensteuerung rs_master_slave_flipflop_mit_positiver_taktflankensteuerung_1 (
    .S(D), .C(C), .R(not_1_out), .Q(Q), .nQ(nQ));
endmodule

module _3_Bit_Schieberegister__Kap__3__S__47 (
  input  in_1,
  input  in_2,
  output out_3,
  output out_4,
  output out_5,
  output out_6,
  output out_7,
  output out_8
);

  D_Master_Slave_Flipflop_mit_Taktflankensteuerung__Kap__3__S__41 d_master_slave_flipflop_mit_taktflankensteuerung_kap_3_s_41_1 (
    .D(in_1), .C(in_2), .Q(out_3));  // open: nQ
  D_Master_Slave_Flipflop_mit_Taktflankensteuerung__Kap__3__S__41 d_master_slave_flipflop_mit_taktflankensteuerung_kap_3_s_41_2 (
    .D(out_3), .C(in_2), .Q(out_5));  // open: nQ
  D_Master_Slave_Flipflop_mit_Taktflankensteuerung__Kap__3__S__41 d_master_slave_flipflop_mit_taktflankensteuerung_kap_3_s_41_3 (
    .D(out_5), .C(in_2), .Q(out_7));  // open: nQ
  D_Flipflop_mit_Pegelsteuerung__Kap__3__S__34 d_flipflop_mit_pegelsteuerung_kap_3_s_34_1 (
    .D(in_1), .C(in_2), .Q(out_4));  // open: nQ
  D_Flipflop_mit_Pegelsteuerung__Kap__3__S__34 d_flipflop_mit_pegelsteuerung_kap_3_s_34_2 (
    .D(out_4), .C(in_2), .Q(out_6));  // open: nQ
  D_Flipflop_mit_Pegelsteuerung__Kap__3__S__34 d_flipflop_mit_pegelsteuerung_kap_3_s_34_3 (
    .D(out_6), .C(in_2), .Q(out_8));  // open: nQ
endmodule

module \Übungsblatt_2__Aufgabe_2  (
  input  x,
  input  y,
  input  z,
  output out_4
);

  wire and_1_out, and_2_out, or_1_out, or_2_out;

  or or_1 (or_1_out, ~x, y);  // OR_Gate
  or or_2 (or_2_out, ~y, x);  // OR_Gate
  and and_1 (and_1_out, or_1_out, ~z);  // AND_Gate
  and and_2 (and_2_out, z, or_2_out);
  or or_3 (out_4, and_1_out, and_2_out);
endmodule

module \Übungsblatt_3__Aufgabe_1__Ripple_Carry_Addierer  (
  input  x2,
  input  x1,
  input  x0,
  input  y1,
  input  y0,
  output S3,
  output S2,
  output S1,
  output S0
);

  wire halbaddierer_kap_2_s_80_2_c, volladdierer_kap_2_s_81_1_c_2;

  Halbaddierer__Kap__2__S__80 halbaddierer_kap_2_s_80_1 (.a(x2), .b(volladdierer_kap_2_s_81_1_c_2), .S(S2), .C(S3));
  Volladdierer__Kap__2__S__81 volladdierer_kap_2_s_81_1 (
    .a(x1), .b(y1), .c(halbaddierer_kap_2_s_80_2_c), .C_2(volladdierer_kap_2_s_81_1_c_2), .S(S1));
  Halbaddierer__Kap__2__S__80 halbaddierer_kap_2_s_80_2 (.a(x0), .b(y0), .S(S0), .C(halbaddierer_kap_2_s_80_2_c));
endmodule

module \Übungsblatt_3__Aufgabe_2b__1_Bit_Vergleicher__Version_1  (
  input  a,
  input  b,
  output a_b,
  output a_b_2,
  output a_b_3
);

  _4_1_Multiplexer u_4_1_multiplexer (.e0(1'b0), .e1(1'b0), .e2(1'b1), .e3(1'b0), .out_7(a_b), .s0(a), .s1(b));
  _4_1_Multiplexer u_4_1_multiplexer_2 (.e0(1'b1), .e1(1'b0), .e2(1'b0), .e3(1'b1), .out_7(a_b_2), .s0(a), .s1(b));
  _4_1_Multiplexer u_4_1_multiplexer_3 (.e0(1'b0), .e1(1'b1), .e2(1'b0), .e3(1'b0), .out_7(a_b_3), .s0(a), .s1(b));
endmodule

module \Übungsblatt_3__Aufgabe_2b__1_Bit_Vergleicher__Version_2  (
  input  a,
  input  b,
  output a_b,
  output a_b_2,
  output a_b_3
);

  _4_1_Multiplexer u_4_1_multiplexer (.e0(1'b0), .e1(1'b0), .e2(1'b1), .e3(1'b0), .out_7(a_b), .s0(a), .s1(b));
  _4_1_Multiplexer u_4_1_multiplexer_2 (.e0(1'b1), .e1(1'b0), .e2(1'b0), .e3(1'b1), .out_7(a_b_2), .s0(a), .s1(b));
  _4_1_Multiplexer u_4_1_multiplexer_3 (.e0(1'b0), .e1(1'b1), .e2(1'b0), .e3(1'b0), .out_7(a_b_3), .s0(a), .s1(b));
endmodule

module \Übungsblatt_3__Aufgabe_2c__2_Bit_Vergleicher  (
  input  x1,
  input  x0,
  input  y1,
  input  y0,
  output x_y,
  output x_y_2,
  output x_y_3
);

  wire and_1_out, and_3_out, x0y0_a_b, x0y0_a_b_2, x0y0_a_b_3, x1y1_a_b, x1y1_a_b_2, x1y1_a_b_3;

  \Übungsblatt_3__Aufgabe_2b__1_Bit_Vergleicher__Version_2  x1y1 (
    .a_b(x1y1_a_b), .a_b_2(x1y1_a_b_2), .a_b_3(x1y1_a_b_3), .a(x1), .b(y1));
  \Übungsblatt_3__Aufgabe_2b__1_Bit_Vergleicher__Version_2  x0y0 (
    .a_b(x0y0_a_b), .a_b_2(x0y0_a_b_2), .a_b_3(x0y0_a_b_3), .a(x0), .b(y0));
  and and_1 (and_1_out, x1y1_a_b_2, x0y0_a_b);
  and and_2 (x_y_2, x1y1_a_b_2, x0y0_a_b_2);
  and and_3 (and_3_out, x1y1_a_b_2, x0y0_a_b_3);
  or or_1 (x_y, x1y1_a_b, and_1_out);
  or or_2 (x_y_3, x1y1_a_b_3, and_3_out);
endmodule

module \Übungsblatt_3__Aufgabe_3__Multiplizierer__Version_1  (
  input  a2,
  input  a1,
  input  a0,
  input  b0,
  input  b1,
  input  b2,
  output p5,
  output p4,
  output p3,
  output p2,
  output p1,
  output p0
);

  wire a0b0_out, a0b1_out, a0b2_out, a1b0_out, a1b1_out, a1b2_out, a2b0_out, a2b1_out, a2b2_out,
       volladdierer_kap_2_s_81_2_c_2, volladdierer_kap_2_s_81_2_s, volladdierer_kap_2_s_81_3_c_2,
       volladdierer_kap_2_s_81_4_c_2, volladdierer_kap_2_s_81_4_s, volladdierer_kap_2_s_81_5_c_2,
       volladdierer_kap_2_s_81_5_s, volladdierer_kap_2_s_81_6_c_2, volladdierer_kap_2_s_81_6_s,
       volladdierer_kap_2_s_81_7_c_2, volladdierer_kap_2_s_81_8_c_2, volladdierer_kap_2_s_81_9_c_2;

  and a2b2 (a2b2_out, b2, a2);
  and a2b1 (a2b1_out, b1, a2);
  Volladdierer__Kap__2__S__81 volladdierer_kap_2_s_81_1 (
    .a(volladdierer_kap_2_s_81_2_c_2), .b(a2b2_out), .c(volladdierer_kap_2_s_81_3_c_2), .C_2(p5), .S(p4));
  and a2b0 (a2b0_out, b0, a2);
  Volladdierer__Kap__2__S__81 volladdierer_kap_2_s_81_2 (
    .a(volladdierer_kap_2_s_81_4_c_2), .b(a2b1_out), .c(volladdierer_kap_2_s_81_5_c_2),
    .C_2(volladdierer_kap_2_s_81_2_c_2), .S(volladdierer_kap_2_s_81_2_s));
  and a1b2 (a1b2_out, b2, a1);
  Volladdierer__Kap__2__S__81 volladdierer_kap_2_s_81_3 (
    .a(volladdierer_kap_2_s_81_2_s), .b(a1b2_out), .c(volladdierer_kap_2_s_81_7_c_2),
    .C_2(volladdierer_kap_2_s_81_3_c_2), .S(p3));
  Volladdierer__Kap__2__S__81 volladdierer_kap_2_s_81_4 (
    .a(1'b0), .b(a2b0_out), .c(volladdierer_kap_2_s_81_6_c_2), .C_2(volladdierer_kap_2_s_81_4_c_2),
    .S(volladdierer_kap_2_s_81_4_s));
  and a1b1 (a1b1_out, b1, a1);
  Volladdierer__Kap__2__S__81 volladdierer_kap_2_s_81_5 (
    .a(volladdierer_kap_2_s_81_4_s), .b(a1b1_out), .c(volladdierer_kap_2_s_81_8_c_2),
    .C_2(volladdierer_kap_2_s_81_5_c_2), .S(volladdierer_kap_2_s_81_5_s));
  and a0b2 (a0b2_out, b2, a0);
  and a1b0 (a1b0_out, b0, a1);
  Volladdierer__Kap__2__S__81 volladdierer_kap_2_s_81_6 (
    .a(1'b0), .b(a1b0_out), .c(volladdierer_kap_2_s_81_9_c_2), .C_2(volladdierer_kap_2_s_81_6_c_2),
    .S(volladdierer_kap_2_s_81_6_s));
  and a0b1 (a0b1_out, b1, a0);
  Volladdierer__Kap__2__S__81 volladdierer_kap_2_s_81_7 (
    .a(volladdierer_kap_2_s_81_5_s), .b(a0b2_out), .c(1'b0), .C_2(volladdierer_kap_2_s_81_7_c_2), .S(p2));
  and a0b0 (a0b0_out, b0, a0);
  Volladdierer__Kap__2__S__81 volladdierer_kap_2_s_81_8 (
    .a(volladdierer_kap_2_s_81_6_s), .b(a0b1_out), .c(1'b0), .C_2(volladdierer_kap_2_s_81_8_c_2), .S(p1));
  Volladdierer__Kap__2__S__81 volladdierer_kap_2_s_81_9 (
    .a(1'b0), .b(a0b0_out), .c(1'b0), .C_2(volladdierer_kap_2_s_81_9_c_2), .S(p0));

  // Notes on the sheet:
  //   Kap. 2, Seite 89
endmodule

module \Übungsblatt_3__Aufgabe_3__Multiplizierer__Version_2  (
  input  a2,
  input  a1,
  input  a0,
  input  b2,
  input  b1,
  input  b0,
  output m3,
  output m2,
  output m3_2,
  output m2_2,
  output m1,
  output m0
);

  wire a0b1_out, a0b2_out, a1b0_out, a1b1_out, a1b2_out, a2b0_out, a2b1_out, a2b2_out,
       halbaddierer_kap_2_s_80_1_c, halbaddierer_kap_2_s_80_1_s, halbaddierer_kap_2_s_80_2_c,
       halbaddierer_kap_2_s_80_3_c, volladdierer_kap_2_s_81_2_c_2, volladdierer_kap_2_s_81_3_c_2,
       volladdierer_kap_2_s_81_3_s;

  and a2b2 (a2b2_out, b2, a2);
  and a1b2 (a1b2_out, b2, a1);
  and a0b2 (a0b2_out, b2, a0);
  Volladdierer__Kap__2__S__81 volladdierer_kap_2_s_81_1 (
    .a(a2b2_out), .b(halbaddierer_kap_2_s_80_1_c), .c(volladdierer_kap_2_s_81_2_c_2), .C_2(m3), .S(m2));
  and a1b1 (a1b1_out, b1, a1);
  and a2b1 (a2b1_out, b1, a2);
  Halbaddierer__Kap__2__S__80 halbaddierer_kap_2_s_80_1 (
    .a(a2b1_out), .b(volladdierer_kap_2_s_81_3_c_2), .S(halbaddierer_kap_2_s_80_1_s),
    .C(halbaddierer_kap_2_s_80_1_c));
  Volladdierer__Kap__2__S__81 volladdierer_kap_2_s_81_2 (
    .a(a1b2_out), .b(halbaddierer_kap_2_s_80_1_s), .c(halbaddierer_kap_2_s_80_2_c),
    .C_2(volladdierer_kap_2_s_81_2_c_2), .S(m3_2));
  and a0b1 (a0b1_out, b1, a0);
  Volladdierer__Kap__2__S__81 volladdierer_kap_2_s_81_3 (
    .a(a1b1_out), .b(a2b0_out), .c(halbaddierer_kap_2_s_80_3_c), .C_2(volladdierer_kap_2_s_81_3_c_2),
    .S(volladdierer_kap_2_s_81_3_s));
  Halbaddierer__Kap__2__S__80 halbaddierer_kap_2_s_80_2 (
    .a(a0b2_out), .b(volladdierer_kap_2_s_81_3_s), .S(m2_2), .C(halbaddierer_kap_2_s_80_2_c));
  and a2b0 (a2b0_out, b0, a2);
  and a0b0 (m0, b0, a0);
  and a1b0 (a1b0_out, b0, a1);
  Halbaddierer__Kap__2__S__80 halbaddierer_kap_2_s_80_3 (
    .a(a0b1_out), .b(a1b0_out), .S(m1), .C(halbaddierer_kap_2_s_80_3_c));
endmodule

module \Übungsblatt_3__Aufgabe_4__Schaltwerk  (
  input  S,
  input  R,
  output Q,
  output nQ
);

  nand nand_1 (Q, S, nQ);
  nand nand_2 (nQ, Q, R);
endmodule

module \Übungsblatt_4__Aufgabe_2__JK_Flipflop  (
  output Q2,
  output Q1,
  output Q0
);

  wire _0_qn, _1_qn, _2_qn, Clock_out;

  Clock Clock (.out(Clock_out));
  J_K_Flip_Flop _2 (.J(_0_qn), .clk(Clock_out), .K(Q0), .Q(Q2), .Qn(_2_qn));  // open: preset, en, reset
  J_K_Flip_Flop _1 (.J(Q2), .clk(Clock_out), .K(_2_qn), .Q(Q1), .Qn(_1_qn));  // open: preset, en, reset
  J_K_Flip_Flop _0 (.J(Q1), .clk(Clock_out), .K(_1_qn), .Q(Q0), .Qn(_0_qn));  // open: preset, en, reset
endmodule
